// Logisim project contadorCrescenteDecrescente.circ as structural Verilog: 1 circuit, main circuit main
module main (
  input  in_1
);

  wire and_1_out, and_2_out, and_3_out, and_4_out, and_5_out, and_6_out, and_7_out, and_8_out, and_9_out,
       and_10_out, clock_1_out, D, j_k_ff_1_qn, j_k_ff_3_qn, not_2_out, not_3_out, or_1_out, or_2_out, Q0,
       Q1, Q2, Q3, U;

  Multiplexer multiplexer_1 (.in0(1'b1), .in1(1'b0), .out(U), .sel(in_1));
  Clock clock_1 (.out(clock_1_out));
  not not_1 (D, U);
  J_K_Flip_Flop j_k_ff_1 (.J(1'b1), .K(1'b1), .clk(clock_1_out), .Q(Q0), .Qn(j_k_ff_1_qn));  // open: preset, reset
  Hex_Digit_Display hex_digit_display_1 (.value({Q3, Q2, Q1, Q0}));  // open: dp
  not not_2 (not_2_out, Q0);
  not not_3 (not_3_out, Q1);
  and and_1 (and_1_out, Q0, U);
  and and_2 (and_2_out, D, j_k_ff_1_qn);
  and and_3 (and_3_out, not_2_out, not_3_out);
  or or_1 (or_1_out, and_1_out, and_2_out);
  J_K_Flip_Flop j_k_ff_2 (.J(or_1_out), .K(or_1_out), .clk(clock_1_out), .Q(Q1));  // open: Qn, preset, reset
  and and_4 (and_4_out, Q0, Q1);
  and and_5 (and_5_out, and_4_out, U);
  and and_6 (and_6_out, D, and_3_out);
  J_K_Flip_Flop j_k_ff_3 (
    .J(or_2_out), .K(or_2_out), .clk(clock_1_out), .Q(Q2), .Qn(j_k_ff_3_qn));  // open: preset, reset
  or or_2 (or_2_out, and_5_out, and_6_out);
  and and_7 (and_7_out, and_4_out, Q2);
  and and_8 (and_8_out, j_k_ff_3_qn, and_3_out);
  and and_9 (and_9_out, and_7_out, U);
  or or_3 (and_7_out, and_9_out, and_10_out);
  and and_10 (and_10_out, D, and_8_out);
  J_K_Flip_Flop j_k_ff_4 (.J(and_7_out), .K(and_7_out), .clk(clock_1_out), .Q(Q3));  // open: Qn, preset, reset
endmodule
