// Logisim project contadorNumerosPares.circ as structural Verilog: 2 circuits, main circuit main
module main (
);

  wire and_1_out, clock_1_out, display_1_a, display_1_b, display_1_c, display_1_d, display_1_e, display_1_f,
       display_1_g, not_1_out, Q1, Q2, Q3, Q4;

  J_K_Flip_Flop j_k_ff_1 (.J(1'b0), .K(1'b0), .clk(clock_1_out), .Q(Q4));  // open: Qn, preset, reset
  Clock clock_1 (.out(clock_1_out));
  not not_1 (not_1_out, Q1);
  J_K_Flip_Flop j_k_ff_2 (.J(not_1_out), .K(1'b1), .clk(clock_1_out), .Q(Q3));  // open: Qn, preset, reset
  Display display_1 (
    .B1(Q1), .B2(Q2), .B3(Q3), .B4(Q4), .a(display_1_a), .b(display_1_b), .c(display_1_c), .d(display_1_d),
    .e(display_1_e), .f(display_1_f), .g(display_1_g));
  J_K_Flip_Flop j_k_ff_3 (.J(Q3), .K(Q3), .clk(clock_1_out), .Q(Q2));  // open: Qn, preset, reset
  _7_Segment_Display #(.active("false"), .decimalPoint("false")) u_7_segment_display_1 (
    .g(display_1_g), .f(display_1_f), .a(display_1_a), .b(display_1_b), .e(display_1_e), .d(display_1_d),
    .c(display_1_c));
  and and_1 (and_1_out, Q2, Q3);
  J_K_Flip_Flop j_k_ff_4 (.J(and_1_out), .K(1'b1), .clk(clock_1_out), .Q(Q1));  // open: Qn, preset, reset
endmodule

module Display (
  input  B1,
  input  B2,
  input  B3,
  input  B4,
  output a,
  output b,
  output c,
  output d,
  output e,
  output f,
  output g
);

  wire and_1_out, and_2_out, and_3_out, and_4_out, and_5_out, and_6_out, and_7_out, and_8_out, not_1_out,
       not_2_out, not_3_out, or_1_out, or_2_out, or_3_out, or_4_out, or_5_out, or_6_out, or_7_out, or_8_out,
       xnor_1_out, xnor_2_out, xor_1_out;

  not not_1 (not_1_out, B2);
  not not_2 (not_2_out, B3);
  not not_3 (not_3_out, B4);
  xnor xnor_1 (xnor_1_out, B2, B4);
  xnor xnor_2 (xnor_2_out, B3, B4);
  and and_1 (and_1_out, B3, not_3_out);
  and and_2 (and_2_out, not_1_out, B3);
  and and_3 (and_3_out, not_1_out, not_3_out);
  and and_4 (and_4_out, B2, not_2_out, B4);
  or or_1 (or_1_out, not_1_out, B3);
  and and_5 (and_5_out, not_2_out, not_3_out);
  and and_6 (and_6_out, B2, or_2_out);
  or or_2 (or_2_out, not_2_out, not_3_out);
  xor xor_1 (xor_1_out, B2, B3);
  and and_7 (and_7_out, B3, not_3_out);
  or or_3 (or_3_out, B1, B3, xnor_1_out);
  or or_4 (or_4_out, not_1_out, xnor_2_out);
  or or_5 (or_5_out, B2, not_2_out, B4);
  or or_6 (or_6_out, B1, and_1_out, and_2_out, and_3_out, and_4_out);
  and and_8 (and_8_out, not_3_out, or_1_out);
  or or_7 (or_7_out, B1, and_5_out, and_6_out);
  or or_8 (or_8_out, B1, xor_1_out, and_7_out);
  not not_4 (a, or_3_out);
  not not_5 (b, or_4_out);
  not not_6 (c, or_5_out);
  not not_7 (d, or_6_out);
  not not_8 (e, and_8_out);
  not not_9 (f, or_7_out);
  not not_10 (g, or_8_out);
endmodule
