// Logisim project display.circ as structural Verilog: 1 circuit, main circuit main
module main (
  input  b,
  input  in_2,
  input  in_3,
  input  in_4,
  input  in_5,
  input  a,
  input  f,
  input  g,
  input  e,
  input  d,
  input  c
);

  wire A_t, and_1_out, and_2_out, and_3_out, and_4_out, and_5_out, and_6_out, and_7_out, B_t, C_t, D_t, E_t,
       F_t, G_t, not_1_out, not_2_out, not_3_out, not_4_out, or_1_out, or_2_out, xnor_1_out, xnor_2_out,
       xor_1_out;

  _7_Segment_Display u_7_segment_display_1 (.g(g), .f(f), .a(a), .b(b), .e(e), .d(d), .c(c));  // open: dp
  _7_Segment_Display u_7_segment_display_2 ();  // open: g, f, a, b, e, d, c, dp
  not not_1 (not_1_out, in_2);
  not not_2 (not_2_out, in_3);
  not not_3 (not_3_out, in_4);
  not not_4 (not_4_out, in_5);
  xnor xnor_1 (xnor_1_out, in_3, in_5);
  xnor xnor_2 (xnor_2_out, in_4, in_5);
  and and_1 (and_1_out, in_4, not_4_out);
  and and_2 (and_2_out, not_2_out, in_5);
  and and_3 (and_3_out, not_2_out, not_4_out);
  and and_4 (and_4_out, in_3, not_3_out, in_5);
  or or_1 (or_1_out, not_2_out, in_4);
  and and_5 (and_5_out, not_3_out, not_4_out);
  and and_6 (and_6_out, in_3, or_2_out);
  or or_2 (or_2_out, not_3_out, not_4_out);
  xor xor_1 (xor_1_out, in_3, in_4);
  and and_7 (and_7_out, in_4, not_4_out);
  or or_3 (A_t, in_2, in_4, xnor_1_out);
  or or_4 (B_t, not_2_out, xnor_2_out);
  or or_5 (C_t, in_3, not_3_out, in_5);
  or or_6 (D_t, in_2, and_1_out, and_2_out, and_3_out, and_4_out);
  and and_8 (E_t, not_4_out, or_1_out);
  or or_7 (F_t, in_2, and_5_out, and_6_out);
  or or_8 (G_t, in_2, xor_1_out, and_7_out);
  _7_Segment_Display u_7_segment_display_3 (.g(G_t), .f(F_t), .a(A_t), .b(B_t), .e(E_t), .d(D_t), .c(C_t));  // open: dp

  // Notes on the sheet:
  //   0 = a b c d e f
  //   1 = b c
  //   2 = a b d e g
  //   3 = a b c d g
  //   4 = b c f g
  //   5 = a c d f g
  //   6 = a c d e f g
  //   7 = a b c
  //   8 = a b c d e f g
  //   9 = a b c d f g
  //   g f a b
  //   e d c
  //   B1
  //   B4
endmodule
