// Logisim project douglas-contador-logisimEvolution.circ as structural Verilog: 1 circuit, main circuit main
module main (
);

  wire and_1_out, clock_1_out, d_ff_1_q, not_1_out, or_1_out;
  wire [3:0] j_k_ff_1_q;

  Clock clock_1 (.out(clock_1_out));
  D_Flip_Flop d_ff_1 (.D(1'b1), .clk(clock_1_out), .Q(d_ff_1_q));  // open: Qn, preset, reset
  or or_1 (or_1_out, not_1_out, and_1_out);
  not not_1 (not_1_out, d_ff_1_q);
  J_K_Flip_Flop #(.trigger("falling")) j_k_ff_1 (
    .J(1'b1), .K(1'b1), .clk(clock_1_out), .Q(j_k_ff_1_q[0]), .preset(1'b0), .reset(or_1_out));  // open: Qn
  J_K_Flip_Flop #(.trigger("falling")) j_k_ff_2 (
    .J(1'b1), .K(1'b1), .clk(j_k_ff_1_q[0]), .Q(j_k_ff_1_q[1]), .preset(or_1_out), .reset(1'b0));  // open: Qn
  and and_1 (and_1_out, j_k_ff_1_q[0], j_k_ff_1_q[1], j_k_ff_1_q[3]);
  J_K_Flip_Flop #(.trigger("falling")) j_k_ff_3 (
    .J(1'b1), .K(1'b1), .clk(j_k_ff_1_q[1]), .Q(j_k_ff_1_q[2]), .preset(1'b0), .reset(or_1_out));  // open: Qn
  J_K_Flip_Flop #(.trigger("falling")) j_k_ff_4 (
    .J(1'b1), .K(1'b1), .clk(j_k_ff_1_q[2]), .Q(j_k_ff_1_q[3]), .preset(1'b0), .reset(or_1_out));  // open: Qn
  Hex_Digit_Display hex_digit_display_1 (.value(j_k_ff_1_q));  // open: dp

  // Notes on the sheet:
  //   Faz começar em 2
  //   ff0
  //   ff1
  //   ff2
  //   Reseta para 2 quando chega em 11
  //   ff3
endmodule
