// Logisim project ex02.circ as structural Verilog: 1 circuit, main circuit main
module main (
  input  A,
  input  B,
  input  C,
  output P
);

  wire and_1_out;

  and and_1 (and_1_out, A, B);
  LED led_1 (.in(P));
  or or_1 (P, and_1_out, C);
endmodule
