// Logisim project ex03.circ as structural Verilog: 1 circuit, main circuit main
module main (
  input  A,
  input  B,
  input  C,
  input  D,
  output S
);

  wire and_1_out, or_1_out;

  or or_1 (or_1_out, A, and_1_out);
  and and_1 (and_1_out, B, C);
  and and_2 (S, or_1_out, D);
  LED led_1 (.in(S));
endmodule
