// Logisim project ex04.circ as structural Verilog: 1 circuit, main circuit main
module main (
  input  A,
  input  B,
  input  C,
  input  D,
  output P
);

  LED led_1 (.in(P));
  not not_1 (P, D);
endmodule
