// Logisim project ex05.circ as structural Verilog: 1 circuit, main circuit main
module main (
  input  A,
  input  B,
  input  C,
  input  D,
  output S
);

  wire or_1_out;

  or or_1 (or_1_out, B, C);
  LED led_1 (.in(S));
  and and_1 (S, A, or_1_out);
endmodule
