// Logisim project ex06.circ as structural Verilog: 1 circuit, main circuit main
module main (
  input  A1,
  input  A0,
  input  B1,
  input  B0,
  output G,
  output E,
  output L
);

  wire and_1_out, and_2_out, and_3_out, and_4_out, and_5_out, and_6_out, and_7_out;

  and and_1 (and_1_out, A1, ~B1);  // AND_Gate
  and and_2 (and_2_out, A0, ~B1, ~B0);  // AND_Gate
  and and_3 (and_3_out, A1, A0, ~B0);  // AND_Gate
  and and_4 (and_4_out, ~A1, B1);  // AND_Gate
  and and_5 (and_5_out, ~A1, ~A0, B0);  // AND_Gate
  and and_6 (and_6_out, ~A0, B1, B0);  // AND_Gate
  LED led_1 (.in(G));
  or or_1 (G, and_1_out, and_2_out, and_3_out);
  or or_2 (L, and_4_out, and_5_out, and_6_out);
  LED led_2 (.in(L));
  and and_7 (and_7_out, G, L);
  LED led_3 (.in(E));
  not not_1 (E, and_7_out);
endmodule
