// Logisim project ex07.circ as structural Verilog: 1 circuit, main circuit main
module main (
  input  A,
  input  B,
  input  C,
  output M
);

  LED led_1 (.in(M));
  nor nor_1 (M, A, B, C);
endmodule
