// Logisim project ex08.circ as structural Verilog: 1 circuit, main circuit main
module main (
  input  A,
  input  B,
  input  C,
  output S
);

  wire and_1_out, D_out;

  Button D (.out(D_out));
  and and_1 (and_1_out, A, B, C);
  or or_1 (S, and_1_out, D_out);
  LED led_1 (.in(S));
endmodule
