// Logisim project ex09.circ as structural Verilog: 1 circuit, main circuit main
module main (
  input  A,
  input  B,
  input  S1,
  input  S0,
  output Y
);

  wire and_1_out, and_2_out, and_3_out, and_4_out;

  and and_1 (and_1_out, A, B);
  and and_2 (and_2_out, A, ~S0);  // AND_Gate
  and and_3 (and_3_out, B, ~S1, S0);  // AND_Gate
  and and_4 (and_4_out, B, S1, ~S0);  // AND_Gate
  or or_1 (Y, and_1_out, and_2_out, and_3_out, and_4_out);
  LED led_1 (.in(Y));
endmodule
