// Logisim project ex10.circ as structural Verilog: 1 circuit, main circuit main
module main (
  input  A,
  input  B,
  input  C,
  input  D,
  output S1,
  output S2,
  output S3
);

  wire and_1_out, and_2_out, and_3_out, not_1_out, or_1_out;

  not not_1 (not_1_out, D);
  or or_1 (or_1_out, C, B, A);
  and and_1 (and_1_out, C, B);
  and and_2 (and_2_out, C, A);
  and and_3 (and_3_out, B, A);
  and and_4 (S1, not_1_out, or_1_out);
  or or_2 (S3, and_1_out, and_2_out, and_3_out);
  LED led_1 (.in(S1));
  LED led_2 (.in(D));
  LED led_3 (.in(S3));

  assign S2 = D;
endmodule
