// Logisim project ex01.circ as structural Verilog: 4 circuits, main circuit main
module main (
);

  wire button_1_out, timer4_1_o, timer5_1_done, timer5_1_o, timer8_1_done, timer8_1_o;

  Button button_1 (.out(button_1_out));
  LED led_1 (.in(timer5_1_o));
  timer5 timer5_1 (.I(button_1_out), .done(timer5_1_done), .O(timer5_1_o));
  LED led_2 (.in(timer8_1_o));
  timer8 timer8_1 (.I(timer5_1_done), .done(timer8_1_done), .O(timer8_1_o));
  LED led_3 (.in(timer4_1_o));
  timer4 timer4_1 (.I(timer8_1_done), .O(timer4_1_o));  // open: done

  // Notes on the sheet:
  //   Entrada
  //   Região Central
  //   Saida
endmodule

module timer5 (
  input  I,
  output O,
  output done
);

  wire and_1_out, clock_1_out, j_k_ff_2_q, j_k_ff_3_q, j_k_ff_4_q, reset;

  J_K_Flip_Flop j_k_ff_1 (.Q(O), .preset(I), .reset(done));  // open: J, K, clk, Qn
  not not_1 (reset, O);
  Clock clock_1 (.out(clock_1_out));
  J_K_Flip_Flop j_k_ff_2 (.J(1'b1), .K(1'b1), .clk(clock_1_out), .Q(j_k_ff_2_q), .reset(reset));  // open: Qn, preset
  J_K_Flip_Flop j_k_ff_3 (
    .J(j_k_ff_2_q), .K(j_k_ff_2_q), .clk(clock_1_out), .Q(j_k_ff_3_q), .reset(reset));  // open: Qn, preset
  and and_1 (and_1_out, j_k_ff_2_q, j_k_ff_3_q);
  J_K_Flip_Flop j_k_ff_4 (
    .J(and_1_out), .K(and_1_out), .clk(clock_1_out), .Q(j_k_ff_4_q), .reset(reset));  // open: Qn, preset
  and and_2 (done, j_k_ff_2_q, j_k_ff_4_q);

  // Other names for the same wires on the sheet: is_5 = done
endmodule

module timer8 (
  input  I,
  output O,
  output done
);

  wire and_1_out, and_2_out, clock_1_out, j_k_ff_2_q, j_k_ff_3_q, j_k_ff_4_q, reset;

  J_K_Flip_Flop j_k_ff_1 (.Q(O), .preset(I), .reset(done));  // open: J, K, clk, Qn
  not not_1 (reset, O);
  J_K_Flip_Flop j_k_ff_2 (.J(1'b1), .K(1'b1), .clk(clock_1_out), .Q(j_k_ff_2_q), .reset(reset));  // open: Qn, preset
  Clock clock_1 (.out(clock_1_out));
  J_K_Flip_Flop j_k_ff_3 (
    .J(j_k_ff_2_q), .K(j_k_ff_2_q), .clk(clock_1_out), .Q(j_k_ff_3_q), .reset(reset));  // open: Qn, preset
  and and_1 (and_1_out, j_k_ff_2_q, j_k_ff_3_q);
  J_K_Flip_Flop j_k_ff_4 (
    .J(and_1_out), .K(and_1_out), .clk(clock_1_out), .Q(j_k_ff_4_q), .reset(reset));  // open: Qn, preset
  and and_2 (and_2_out, and_1_out, j_k_ff_4_q);
  J_K_Flip_Flop j_k_ff_5 (
    .J(and_2_out), .K(and_2_out), .clk(clock_1_out), .Q(done), .reset(reset));  // open: Qn, preset

  // Other names for the same wires on the sheet: is_8 = done
endmodule

module timer4 (
  input  I,
  output O,
  output done
);

  wire and_1_out, clock_1_out, j_k_ff_2_q, j_k_ff_3_q, reset;

  J_K_Flip_Flop j_k_ff_1 (.Q(O), .preset(I), .reset(done));  // open: J, K, clk, Qn
  not not_1 (reset, O);
  J_K_Flip_Flop j_k_ff_2 (.J(1'b1), .K(1'b1), .clk(clock_1_out), .Q(j_k_ff_2_q), .reset(reset));  // open: Qn, preset
  Clock clock_1 (.out(clock_1_out));
  J_K_Flip_Flop j_k_ff_3 (
    .J(j_k_ff_2_q), .K(j_k_ff_2_q), .clk(clock_1_out), .Q(j_k_ff_3_q), .reset(reset));  // open: Qn, preset
  and and_1 (and_1_out, j_k_ff_2_q, j_k_ff_3_q);
  J_K_Flip_Flop j_k_ff_4 (
    .J(and_1_out), .K(and_1_out), .clk(clock_1_out), .Q(done), .reset(reset));  // open: Qn, preset

  // Other names for the same wires on the sheet: is_4 = done
endmodule
