// Logisim project ex04.circ as structural Verilog: 4 circuits, main circuit main
module main (
);

  wire button_1_out, timer3_1_done, timer5_1_done, timer5_1_o, timer5_2_o, timer10_1_done, timer10_1_o;

  Button button_1 (.out(button_1_out));
  LED led_1 (.in(timer5_1_o));
  timer5 timer5_1 (.I(button_1_out), .done(timer5_1_done), .O(timer5_1_o));
  timer3 timer3_1 (.I(timer5_1_done), .done(timer3_1_done));  // open: O
  LED led_2 (.in(timer10_1_o));
  timer10 timer10_1 (.I(timer3_1_done), .done(timer10_1_done), .O(timer10_1_o));
  LED led_3 (.in(timer5_2_o));
  timer5 timer5_2 (.I(timer10_1_done), .O(timer5_2_o));  // open: done

  // Notes on the sheet:
  //   Porta
  //   Espera
  //   Camera
  //   Luz Indicadora
endmodule

module timer3 (
  input  I,
  output O,
  output done
);

  wire clock_1_out, j_k_ff_2_q, j_k_ff_3_q, reset;

  J_K_Flip_Flop j_k_ff_1 (.Q(O), .preset(I), .reset(done));  // open: J, K, clk, Qn
  not not_1 (reset, O);
  J_K_Flip_Flop j_k_ff_2 (.J(1'b1), .K(1'b1), .clk(clock_1_out), .Q(j_k_ff_2_q), .reset(reset));  // open: Qn, preset
  Clock clock_1 (.out(clock_1_out));
  J_K_Flip_Flop j_k_ff_3 (
    .J(j_k_ff_2_q), .K(j_k_ff_2_q), .clk(clock_1_out), .Q(j_k_ff_3_q), .reset(reset));  // open: Qn, preset
  and and_1 (done, j_k_ff_2_q, j_k_ff_3_q);

  // Other names for the same wires on the sheet: is_3 = done
endmodule

module timer5 (
  input  I,
  output O,
  output done
);

  wire and_1_out, clock_1_out, j_k_ff_2_q, j_k_ff_3_q, j_k_ff_4_q, reset;

  J_K_Flip_Flop j_k_ff_1 (.Q(O), .preset(I), .reset(done));  // open: J, K, clk, Qn
  not not_1 (reset, O);
  J_K_Flip_Flop j_k_ff_2 (.J(1'b1), .K(1'b1), .clk(clock_1_out), .Q(j_k_ff_2_q), .reset(reset));  // open: Qn, preset
  Clock clock_1 (.out(clock_1_out));
  J_K_Flip_Flop j_k_ff_3 (
    .J(j_k_ff_2_q), .K(j_k_ff_2_q), .clk(clock_1_out), .Q(j_k_ff_3_q), .reset(reset));  // open: Qn, preset
  and and_1 (and_1_out, j_k_ff_2_q, j_k_ff_3_q);
  J_K_Flip_Flop j_k_ff_4 (
    .J(and_1_out), .K(and_1_out), .clk(clock_1_out), .Q(j_k_ff_4_q), .reset(reset));  // open: Qn, preset
  and and_2 (done, j_k_ff_2_q, j_k_ff_4_q);

  // Other names for the same wires on the sheet: is_5 = done
endmodule

module timer10 (
  input  I,
  output O,
  output done
);

  wire and_1_out, and_2_out, clock_1_out, j_k_ff_2_q, j_k_ff_3_q, j_k_ff_4_q, j_k_ff_5_q, reset;

  J_K_Flip_Flop j_k_ff_1 (.Q(O), .preset(I), .reset(done));  // open: J, K, clk, Qn
  not not_1 (reset, O);
  J_K_Flip_Flop j_k_ff_2 (.J(1'b1), .K(1'b1), .clk(clock_1_out), .Q(j_k_ff_2_q), .reset(reset));  // open: Qn, preset
  Clock clock_1 (.out(clock_1_out));
  J_K_Flip_Flop j_k_ff_3 (
    .J(j_k_ff_2_q), .K(j_k_ff_2_q), .clk(clock_1_out), .Q(j_k_ff_3_q), .reset(reset));  // open: Qn, preset
  and and_1 (and_1_out, j_k_ff_2_q, j_k_ff_3_q);
  J_K_Flip_Flop j_k_ff_4 (
    .J(and_1_out), .K(and_1_out), .clk(clock_1_out), .Q(j_k_ff_4_q), .reset(reset));  // open: Qn, preset
  and and_2 (and_2_out, and_1_out, j_k_ff_4_q);
  J_K_Flip_Flop j_k_ff_5 (
    .J(and_2_out), .K(and_2_out), .clk(clock_1_out), .Q(j_k_ff_5_q), .reset(reset));  // open: Qn, preset
  and and_3 (done, j_k_ff_3_q, j_k_ff_5_q);

  // Other names for the same wires on the sheet: is_10 = done
endmodule
