// Logisim project listaExercicios.circ as structural Verilog: 11 circuits, main circuit ex01
module ex01 (
);

  wire and_1_out, clock_1_out, ex06_1_a, ex06_1_b, ex06_1_c, ex06_1_d, ex06_1_e, ex06_1_f, ex06_1_g,
       j_k_ff_1_qn, j_k_ff_2_qn, j_k_ff_3_qn, Q0, Q1, Q2, Q3;

  Clock clock_1 (.out(clock_1_out));
  J_K_Flip_Flop j_k_ff_1 (
    .J(1'b1), .K(1'b1), .clk(clock_1_out), .Q(Q0), .Qn(j_k_ff_1_qn), .reset(and_1_out));  // open: preset
  J_K_Flip_Flop j_k_ff_2 (
    .J(1'b1), .K(1'b1), .clk(j_k_ff_1_qn), .Q(Q1), .Qn(j_k_ff_2_qn), .reset(and_1_out));  // open: preset
  and and_1 (and_1_out, Q1, Q3);
  J_K_Flip_Flop j_k_ff_3 (
    .J(1'b1), .K(1'b1), .clk(j_k_ff_2_qn), .Q(Q2), .Qn(j_k_ff_3_qn), .reset(and_1_out));  // open: preset
  J_K_Flip_Flop j_k_ff_4 (.J(1'b1), .K(1'b1), .clk(j_k_ff_3_qn), .Q(Q3), .reset(and_1_out));  // open: Qn, preset
  ex06 ex06_1 (
    .B3(Q3), .B2(Q2), .B1(Q1), .B0(Q0), .g(ex06_1_g), .a(ex06_1_a), .b(ex06_1_b), .c(ex06_1_c), .d(ex06_1_d),
    .e(ex06_1_e), .f(ex06_1_f));
  _7_Segment_Display #(.decimalPoint("false")) u_7_segment_display_1 (
    .g(ex06_1_g), .f(ex06_1_f), .a(ex06_1_a), .b(ex06_1_b), .e(ex06_1_e), .d(ex06_1_d), .c(ex06_1_c));

  // Notes on the sheet:
  //   Exercicio 01: contador assincrono MOD 10
endmodule

module ex02 (
  input  in_1
);

  wire and_1_out, and_2_out, and_3_out, and_4_out, clock_1_out, ex06_1_a, ex06_1_b, ex06_1_c, ex06_1_d,
       ex06_1_e, ex06_1_f, ex06_1_g, J1, J2, not_1_out, not_2_out, not_3_out, not_4_out, not_5_out, Q0, Q1,
       Q2;

  Clock clock_1 (.out(clock_1_out));
  J_K_Flip_Flop j_k_ff_1 (.J(1'b1), .K(1'b1), .clk(clock_1_out), .Q(Q0));  // open: Qn, preset, reset
  not not_1 (not_1_out, in_1);
  not not_2 (not_2_out, Q0);
  and and_1 (and_1_out, not_1_out, not_2_out);
  and and_2 (and_2_out, in_1, Q0);
  J_K_Flip_Flop j_k_ff_2 (.J(J1), .K(J1), .clk(clock_1_out), .Q(Q1));  // open: Qn, preset, reset
  or or_1 (J1, and_1_out, and_2_out);
  J_K_Flip_Flop j_k_ff_3 (.J(J2), .K(J2), .clk(clock_1_out), .Q(Q2));  // open: Qn, preset, reset
  not not_3 (not_3_out, in_1);
  not not_4 (not_4_out, Q0);
  not not_5 (not_5_out, Q1);
  and and_3 (and_3_out, not_3_out, not_4_out, not_5_out);
  and and_4 (and_4_out, in_1, Q0, Q1);
  or or_2 (J2, and_3_out, and_4_out);
  ex06 ex06_1 (
    .B3(1'b0), .B2(Q2), .B1(Q1), .B0(Q0), .g(ex06_1_g), .a(ex06_1_a), .b(ex06_1_b), .c(ex06_1_c),
    .d(ex06_1_d), .e(ex06_1_e), .f(ex06_1_f));
  _7_Segment_Display #(.decimalPoint("false")) u_7_segment_display_1 (
    .g(ex06_1_g), .f(ex06_1_f), .a(ex06_1_a), .b(ex06_1_b), .e(ex06_1_e), .d(ex06_1_d), .c(ex06_1_c));

  // Other names for the same wires on the sheet: K1 = J1; K2 = J2; U_D = in_1

  // Notes on the sheet:
  //   Exercicio 02: Contador sincrono de 3 bits com controle Up/Down
endmodule

module ex03 (
  input  in_1,
  output out_2
);

  wire clock_1_out, d_ff_1_q, d_ff_2_q, d_ff_3_q;

  Clock clock_1 (.out(clock_1_out));
  D_Flip_Flop d_ff_1 (.D(in_1), .clk(clock_1_out), .Q(d_ff_1_q));  // open: Qn, preset, reset
  D_Flip_Flop d_ff_2 (.D(d_ff_1_q), .clk(clock_1_out), .Q(d_ff_2_q));  // open: Qn, preset, reset
  D_Flip_Flop d_ff_3 (.D(d_ff_2_q), .clk(clock_1_out), .Q(d_ff_3_q));  // open: Qn, preset, reset
  D_Flip_Flop d_ff_4 (.D(d_ff_3_q), .clk(clock_1_out), .Q(out_2));  // open: Qn, preset, reset

  // Notes on the sheet:
  //   Exercicio 03: registrador de deslocamento de 4 bits
endmodule

module ex04 (
  input  D0,
  input  D1,
  input  D2,
  input  D3,
  input  D4,
  input  D5,
  input  D6,
  input  D7,
  input  A,
  input  B,
  input  C,
  output Y
);

  wire and_1_out, and_2_out, and_3_out, and_4_out, and_5_out, and_6_out, and_7_out, and_8_out;

  and and_1 (and_1_out, D0, ~A, ~B, ~C);  // AND_Gate
  and and_2 (and_2_out, D1, ~A, ~B, C);  // AND_Gate
  and and_3 (and_3_out, D2, ~A, B, ~C);  // AND_Gate
  and and_4 (and_4_out, D3, ~A, B, C);  // AND_Gate
  and and_5 (and_5_out, D4, A, ~B, ~C);  // AND_Gate
  and and_6 (and_6_out, D5, A, ~B, C);  // AND_Gate
  and and_7 (and_7_out, D6, A, B, ~C);  // AND_Gate
  and and_8 (and_8_out, D7, A, B, C);
  or or_1 (Y, and_1_out, and_2_out, and_3_out, and_4_out, and_5_out, and_6_out, and_7_out, and_8_out);

  // Other names for the same wires on the sheet: S0 = C; S1 = B; S2 = A
endmodule

module ex05 (
  input  D3,
  input  D2,
  input  D1,
  input  D0,
  output Y1,
  output Y0
);

  wire and_1_out;

  and and_1 (and_1_out, D1, ~D2);  // AND_Gate
  or or_1 (Y0, and_1_out, D3);
  or or_2 (Y1, D2, D3);

  // Notes on the sheet:
  //   Exercicio 05: Codificador Prioritario 4 para 2
endmodule

module ex06 (
  input  B3,
  input  B2,
  input  B1,
  input  B0,
  output a,
  output b,
  output c,
  output d,
  output e,
  output f,
  output g
);

  wire and_1_out, and_2_out, and_3_out, and_4_out, and_5_out, and_6_out, and_7_out, not_1_out, not_2_out,
       not_3_out, or_1_out, or_2_out, xnor_1_out, xnor_2_out, xor_1_out;

  not not_1 (not_1_out, B2);
  not not_2 (not_2_out, B1);
  not not_3 (not_3_out, B0);
  xnor xnor_1 (xnor_1_out, B2, B0);
  xnor xnor_2 (xnor_2_out, B1, B0);
  and and_1 (and_1_out, B1, not_3_out);
  and and_2 (and_2_out, not_1_out, B1);
  and and_3 (and_3_out, not_1_out, not_3_out);
  and and_4 (and_4_out, B2, not_2_out, B0);
  or or_1 (or_1_out, not_1_out, B1);
  and and_5 (and_5_out, not_2_out, not_3_out);
  and and_6 (and_6_out, B2, or_2_out);
  or or_2 (or_2_out, not_2_out, not_3_out);
  xor xor_1 (xor_1_out, B2, B1);
  and and_7 (and_7_out, B1, not_3_out);
  or or_3 (a, B3, B1, xnor_1_out);
  or or_4 (b, not_1_out, xnor_2_out);
  or or_5 (c, B2, not_2_out, B0);
  or or_6 (d, B3, and_1_out, and_2_out, and_3_out, and_4_out);
  and and_8 (e, not_3_out, or_1_out);
  or or_7 (f, B3, and_5_out, and_6_out);
  or or_8 (g, B3, xor_1_out, and_7_out);

  // Notes on the sheet:
  //   Exercicio 06: Decodificador BCD para 7 segmentos
endmodule

module ex07 (
  input  A,
  input  B,
  input  C,
  input  D,
  output F
);

  wire not_1_out, not_2_out, or_1_out, or_2_out;

  not not_1 (not_1_out, B);
  not not_2 (not_2_out, D);
  or or_1 (or_1_out, B, D);
  or or_2 (or_2_out, not_1_out, not_2_out);
  and and_1 (F, or_1_out, or_2_out);

  // Notes on the sheet:
  //   Exercicio 07: Produto da Soma (POS)
endmodule

module ex08 (
  input  A,
  input  B,
  input  C,
  input  D,
  output F
);

  wire and_1_out, and_2_out, and_3_out, not_1_out, not_2_out, not_3_out;

  not not_1 (not_1_out, B);
  not not_2 (not_2_out, C);
  not not_3 (not_3_out, A);
  and and_1 (and_1_out, D, not_1_out);
  and and_2 (and_2_out, D, A);
  and and_3 (and_3_out, not_2_out, B, not_3_out);
  or or_1 (F, and_1_out, and_2_out, and_3_out);

  // Notes on the sheet:
  //   Exercicio 08: Soma de Produtos (SOP)
endmodule

module ex09 (
  input  E,
  output S
);

  wire and_1_out, and_2_out, and_3_out, and_4_out, and_5_out, clock_1_out, D0, D1, D2, Q0, Q1, Q2;

  D_Flip_Flop d_ff_1 (.D(D2), .clk(clock_1_out), .Q(Q2));  // open: Qn, preset, reset
  Clock clock_1 (.out(clock_1_out));
  and and_1 (and_1_out, E, Q1, Q0);
  and and_2 (and_2_out, Q0, ~E);  // AND_Gate
  and and_3 (and_3_out, ~Q0, E, Q1);  // AND_Gate
  and and_4 (and_4_out, ~Q0, E, ~Q2);  // AND_Gate
  and and_5 (and_5_out, Q0, E, ~Q1);  // AND_Gate
  or or_1 (D2, Q2, and_1_out);
  or or_2 (D1, and_2_out, and_3_out);
  or or_3 (D0, and_4_out, and_5_out);
  D_Flip_Flop d_ff_2 (.D(D1), .clk(clock_1_out), .Q(Q1));  // open: Qn, preset, reset
  D_Flip_Flop d_ff_3 (.D(D0), .clk(clock_1_out), .Q(Q0));  // open: Qn, preset, reset
  LED led_1 (.in(S));
  and and_6 (S, ~Q0, ~Q1, Q2);  // AND_Gate

  // Notes on the sheet:
  //   Exercicio 09: Maquina de estado de Moore
  //   Estados:
  //   000 = sequencia vazia
  //   001 = sequencia atual 1
  //   010 = sequencia atual 10
  //   011 = sequencia atual 101
  //   100 = sequencia atual 1011
endmodule

module ex10 (
  input  [1:0] D,
  input  [1:0] C,
  input  [1:0] B,
  input  [1:0] A,
  output [1:0] out_5
);

  wire clk, ex10_mux_1_y, ex10_mux_2_y, Q0, Q1, Y0, Y1, Y2, Y3;

  Clock clock_1 (.out(clk));
  J_K_Flip_Flop j_k_ff_1 (.J(1'b1), .K(1'b1), .clk(clk), .Q(Q0));  // open: Qn, preset, reset
  J_K_Flip_Flop j_k_ff_2 (.J(Q0), .K(Q0), .clk(clk), .Q(Q1));  // open: Qn, preset, reset
  and and_1 (Y3, Q0, Q1);
  and and_2 (Y2, ~Q0, Q1);  // AND_Gate
  and and_3 (Y1, Q0, ~Q1);  // AND_Gate
  and and_4 (Y0, ~Q0, ~Q1);  // AND_Gate
  ex10_Mux ex10_mux_1 (.E1(C[0]), .E2(B[0]), .E3(A[0]), .E0(D[0]), .S1(Q1), .S0(Q0), .Y(ex10_mux_1_y));
  ex10_Mux ex10_mux_2 (.E1(C[1]), .E2(B[1]), .E3(A[1]), .E0(D[1]), .S1(Q1), .S0(Q0), .Y(ex10_mux_2_y));
  D_Flip_Flop d_ff_1 (.D(ex10_mux_1_y), .clk(clk), .Q(out_5[0]));  // open: Qn, preset, reset
  D_Flip_Flop d_ff_2 (.D(ex10_mux_2_y), .clk(clk), .Q(out_5[1]));  // open: Qn, preset, reset

  // Notes on the sheet:
  //   Contador sincrono de 2 bits
  //   Decodificador 2:4
  //   Multiplexador 4:1
  //   Registrador de Saída
endmodule

module ex10_Mux (
  input  E0,
  input  E1,
  input  E2,
  input  E3,
  input  S1,
  input  S0,
  output Y
);

  wire and_1_out, and_2_out, and_3_out, and_4_out;

  and and_1 (and_1_out, E0, ~S1, ~S0);  // AND_Gate
  and and_2 (and_2_out, E1, ~S1, S0);  // AND_Gate
  and and_3 (and_3_out, E2, S1, ~S0);  // AND_Gate
  and and_4 (and_4_out, E3, S1, S0);
  or or_1 (Y, and_1_out, and_2_out, and_3_out, and_4_out);
endmodule
