// Logisim project tortura.circ as structural Verilog: 1 circuit, main circuit main
module main (
);

  wire and_1_out, and_2_out, and_3_out, and_4_out, and_5_out, and_6_out, and_7_out, and_8_out, and_9_out,
       clock_1_out, j_k_ff_3_qn, j_k_ff_4_qn, not_1_out, not_2_out, not_3_out, not_4_out, not_5_out,
       not_6_out, not_7_out, or_1_out, or_2_out, or_3_out, or_4_out;
  wire [3:0] j_k_ff_1_q;

  or or_1 (or_1_out, and_1_out, and_2_out, and_3_out);
  and and_1 (and_1_out, j_k_ff_1_q[3], not_1_out, not_2_out);
  not not_1 (not_1_out, or_3_out);
  not not_2 (not_2_out, j_k_ff_1_q[1]);
  and and_2 (and_2_out, or_3_out, not_3_out);
  not not_3 (not_3_out, j_k_ff_1_q[3]);
  and and_3 (and_3_out, j_k_ff_1_q[1], not_4_out);
  not not_4 (not_4_out, j_k_ff_1_q[3]);
  not not_5 (not_5_out, j_k_ff_4_qn);
  not not_6 (not_6_out, j_k_ff_3_qn);
  and and_4 (and_4_out, not_5_out, not_6_out);
  and and_5 (and_5_out, j_k_ff_3_qn, j_k_ff_4_qn);
  J_K_Flip_Flop j_k_ff_1 (.J(or_1_out), .K(1'b1), .clk(clock_1_out), .Q(j_k_ff_1_q[0]));  // open: Qn, preset, reset
  Clock clock_1 (.out(clock_1_out));
  and and_6 (and_6_out, j_k_ff_1_q[0], not_7_out);
  or or_2 (or_2_out, j_k_ff_1_q[0], and_4_out, and_5_out);
  J_K_Flip_Flop j_k_ff_2 (
    .J(or_2_out), .K(and_6_out), .clk(clock_1_out), .Q(j_k_ff_1_q[1]));  // open: Qn, preset, reset
  and and_7 (and_7_out, j_k_ff_1_q[1], j_k_ff_1_q[0]);
  or or_3 (or_3_out, and_7_out, j_k_ff_1_q[3]);
  not not_7 (not_7_out, j_k_ff_1_q[3]);
  and and_8 (and_8_out, j_k_ff_1_q[0], j_k_ff_1_q[1], not_7_out);
  J_K_Flip_Flop j_k_ff_3 (
    .J(and_8_out), .K(or_3_out), .clk(clock_1_out), .Q(j_k_ff_1_q[2]), .Qn(j_k_ff_3_qn));  // open: preset, reset
  and and_9 (and_9_out, j_k_ff_1_q[0], j_k_ff_1_q[1], j_k_ff_1_q[2]);
  or or_4 (or_4_out, j_k_ff_1_q[0], j_k_ff_1_q[1]);
  J_K_Flip_Flop j_k_ff_4 (
    .J(and_9_out), .K(or_4_out), .clk(clock_1_out), .Q(j_k_ff_1_q[3]), .Qn(j_k_ff_4_qn));  // open: preset, reset
  Hex_Digit_Display hex_digit_display_1 (.value(j_k_ff_1_q));  // open: dp

  // Notes on the sheet:
  //   Q0
  //   Q1
  //   Q2
  //   Q3
endmodule
